# Fritzing sketch MQTTerm (saved by Fritzing 0.9.3b)
breadboards: 1

parts:
  WeMos_D1_Mini1 = WeMos D1 Mini
  U1 = SWITCH_SPDT [package=kps-1290]
  R1 = Resistor [tolerance=±5% resistance=1k package=THT]
  R2 = Resistor [tolerance=±5% resistance=4.7k package=THT]
  DS1 = DS18B20 1-Wire Temperature Sensor [part_number=DS18B20]

nets:
  3V3: WeMos_D1_Mini1.3V3, R2.Pin_1, DS1.VDD
  N1: WeMos_D1_Mini1.D0, R1.Pin_1
  N2: WeMos_D1_Mini1.D1, R2.Pin_0, DS1.DQ
  N3: WeMos_D1_Mini1.D6, U1.P
  N4: WeMos_D1_Mini1.G, U1.O, DS1.GND
  N5: WeMos_D1_Mini1.RST, R1.Pin_0
